# Fritzing sketch PComp_Tutorial_complete (saved by Fritzing 0.9.9b)
breadboards: 1

parts:
  Raspberry_Pi1 = Raspberry Pi B rev2
  IC1 = L293D [package=THT]
  SM2 = 28BYJ-48 Stepper Motor [part_number=28BYJ-48]

nets:
  N1: Raspberry_Pi1.5V, IC1.+Vmotor, IC1.+V
  N2: Raspberry_Pi1.GND, IC1.0V
  N3: Raspberry_Pi1.GPIO_23, IC1.In_4
  N4: Raspberry_Pi1.GPIO_17, IC1.In_2
  N5: Raspberry_Pi1.GPIO_18, IC1.Enable_1, IC1.Enable_2
  N6: Raspberry_Pi1.GPIO_4, IC1.In_1
  N7: Raspberry_Pi1.GPIO_24, IC1.In_3
  N8: IC1.Out_2_(_Controlled_by_Enable_1_), SM2.orange-pin

custom parts:
  28BYJ-48 Stepper Motor: Unipolar Stepper Motor 28BYJ-48 Top coil - pink & orange Bottom coil - blue & yellow Common rail - red Connector pins: blue - pink - yellow - orange - red
